# Fritzing sketch multi_function_display (saved by Fritzing 0.7.10b)
breadboards: 1

parts:
  Arduino1 = Arduino
  LCD1 = LCD screen
  R1 = Rotary Potentiometer (Small) [maximum_resistance=100kΩ]
  R2 = Resistor [resistance=10k tolerance=±5% package=THT]
  S2 = Pushbutton [package=THT]
  R3 = Photocell (LDR) [package=THT]
  R4 = Resistor [tolerance=±5% resistance=220 package=THT]
  T1 = LM35 Temperature Sensor [thermistor_type=NTC package="TO92 [THT]"]  # not connected
  R5 = Resistor [tolerance=±5% resistance=220 package=THT]

nets:
  N1: Arduino1.D12, LCD1.RS
  N2: Arduino1.D11, LCD1.E
  N3: Arduino1.D9, LCD1.LED+
  N4: Arduino1.D7, R2.Pin_1, S2.leg1
  N5: Arduino1.D6, R5.Pin_1
  N6: Arduino1.D5, LCD1.DB4
  N7: Arduino1.D4, LCD1.DB5
  N8: Arduino1.D3, LCD1.DB6
  N9: Arduino1.D2, LCD1.DB7
  +5V: Arduino1.+5V, LCD1.VDD, R1.leg2, S2.leg0, R3.pin_1, R5.Pin_0
  GND: Arduino1.GND, LCD1.VSS, LCD1.R/W, LCD1.LED-, R1.leg1, R2.Pin_0, R4.Pin_1
  N10: Arduino1.A1, R3.pin_0, R4.Pin_0
  N11: LCD1.V0, R1.wiper
